// Digital circuit 8bitcpu.dig as structural Verilog
module _8bitcpu (
  input  CLK_MAIN,
  input  CLK_DISPLAY
);

  wire ADDRLE, AFCY, AFOV, AFZF, ALE, ALUOE, ALUSUB, AOE, BLE, BOE, decoder_1_out_0, decoder_1_out_1,
       decoder_1_out_2, decoder_1_out_3, DISPLE, FCY, FOV, FTCMP, HALT, IRLE, IRLOE, IROE, ManualRAM,
       not_1_out, or_1_out, PCCE, PCIS0, PCIS1, PCIS2, PCOE, PSWFLE, PSWLE, RAMLE, RAMOE, RESERVED0,
       RESERVED1, ROMOE, RST;
  wire [2:0] MCIO;
  wire [3:0] IR_do, IRHO, ManualRAMAddr, multiplexer_1_out, pulldown_1_out, pulldown_1_out_2, RAR_q;
  wire [7:0] ADO, BDO, LUTDISP_d, ManualRAMData, multiplexer_2_out, PC_do, RAM_d, register_with_clear_2_q,
       register_with_clear_3_q, register_with_clear_4_q, register_with_clear_5_q;
  wire [9:0] register_with_clear_1_q;

  Counter #(.Bits(3)) counter_1 (.en(1'b1), .C(CLK_MAIN), .clr(RST), .out(MCIO));  // open: ovf
  Button button_1 (.out(RST));
  EEPROM #(.AddrBits(13), .isProgramMemory("true"), .Bits(8)) LUTDECODE0 (
    .A({{6{1'b0}}, IRHO, MCIO}), .CS(~1'b0), .WE(~1'b1), .OE(~1'b0),
    .D({RAMLE, ADDRLE, PCCE, PCOE, ROMOE, IRLOE, IROE, IRLE}));
  EEPROM #(.AddrBits(13), .isProgramMemory("true"), .Bits(8)) LUTDECODE1 (
    .A({6'b000001, IRHO, MCIO}), .CS(~1'b0), .WE(~1'b1), .OE(~1'b0),
    .D({DISPLE, ALUSUB, ALUOE, BOE, BLE, AOE, ALE, RAMOE}));
  EEPROM #(.AddrBits(13), .isProgramMemory("true"), .Bits(8)) LUTDECODE2 (
    .A({6'b000010, IRHO, MCIO}), .CS(~1'b0), .WE(~1'b1), .OE(~1'b0),
    .D({PCIS2, PCIS1, PCIS0, PSWFLE, PSWLE, RESERVED1, RESERVED0, HALT}));
  DipSwitch dipswitch_1 (.out(ManualRAM));
  DipSwitch dipswitch_2 (.out(ManualRAMData[0]));
  DipSwitch dipswitch_3 (.out(ManualRAMData[1]));
  DipSwitch dipswitch_4 (.out(ManualRAMData[2]));
  DipSwitch dipswitch_5 (.out(ManualRAMData[3]));
  DipSwitch dipswitch_6 (.out(ManualRAMData[4]));
  DipSwitch dipswitch_7 (.out(ManualRAMData[5]));
  DipSwitch dipswitch_8 (.out(ManualRAMData[6]));
  DipSwitch dipswitch_9 (.out(ManualRAMData[7]));
  DipSwitch dipswitch_10 (.out(ManualRAMAddr[0]));
  DipSwitch dipswitch_11 (.out(ManualRAMAddr[1]));
  DipSwitch dipswitch_12 (.out(ManualRAMAddr[2]));
  DipSwitch dipswitch_13 (.out(ManualRAMAddr[3]));
  // Probe on IRLE
  // Probe on IROE
  // Probe on IRLOE
  // Probe on ROMOE
  // Probe on PCOE
  // Probe on PCCE
  // Probe on ADDRLE
  // Probe on RAMLE
  // Probe on RAMOE
  // Probe on ALE
  // Probe on AOE
  // Probe on BLE
  // Probe on BOE
  // Probe on ALUOE
  // Probe on ALUSUB
  // Probe on DISPLE
  // Probe on HALT
  // Probe on RESERVED0
  // Probe on RESERVED1
  // Probe on PSWLE
  // Probe on PSWFLE
  // Probe on PCIS0
  // Probe on PCIS1
  // Probe on PCIS2
  // Probe on ADO
  // Probe on BDO
  // Probe on BDO
  PullDown #(.Bits(8)) pulldown_1 (.out({pulldown_1_out_2, pulldown_1_out}));
  register_with_clear register_with_clear_1 (
    .D({pulldown_1_out_2, pulldown_1_out}), .CLK(CLK_MAIN), .CLR(RST), .LE(DISPLE),
    .Q(register_with_clear_1_q[7:0]));
  registertriout REGA (
    .IO({pulldown_1_out_2, pulldown_1_out}), .CLK(CLK_MAIN), .CLR(RST), .LE(ALE), .OE(AOE), .DO(ADO));
  Register #(.Bits(4)) RAR (.D(pulldown_1_out), .C(CLK_MAIN), .en(ADDRLE), .Q(RAR_q));
  PC PC (
    .IO({pulldown_1_out_2, pulldown_1_out}), .CLK(CLK_MAIN), .CLR(RST), .OE(PCOE), .CE(PCCE),
    .LES({PCIS2, PCIS1, PCIS0}), .FCY(FCY), .FOV(FOV), .FZF(AFZF), .DO(PC_do));
  Counter #(.Bits(2)) CNTSEVENSEG (
    .en(1'b1), .C(CLK_DISPLAY), .clr(decoder_1_out_3), .out(register_with_clear_1_q[9:8]));  // open: ovf
  registertriout REGB (
    .IO({pulldown_1_out_2, pulldown_1_out}), .CLK(CLK_MAIN), .CLR(RST), .LE(BLE), .OE(BOE), .DO(BDO));
  EEPROM #(.AddrBits(8), .isProgramMemory("true"), .Bits(8)) ROM (
    .A(PC_do), .CS(~1'b0), .WE(~1'b1), .OE(~not_1_out), .D({pulldown_1_out_2, pulldown_1_out}));
  not not_1 (not_1_out, ROMOE);
  Multiplexer #(.Bits(4)) multiplexer_1 (.sel(ManualRAM), .in_0(RAR_q), .in_1(ManualRAMAddr), .out(multiplexer_1_out));
  Multiplexer #(.Bits(8)) multiplexer_2 (
    .sel(ManualRAM), .in_0({pulldown_1_out_2, pulldown_1_out}), .in_1(ManualRAMData), .out(multiplexer_2_out));
  EEPROM #(.AddrBits(13), .isProgramMemory("true"), .Bits(8)) LUTDISP (
    .A({2'b00, FTCMP, register_with_clear_1_q}), .CS(~1'b0), .WE(~1'b1), .OE(~1'b0), .D(LUTDISP_d));
  ALU alu_1 (.OE(ALUOE), .A(ADO), .B(BDO), .SUB(ALUSUB), .Y({pulldown_1_out_2, pulldown_1_out}), .CY(AFCY), .OV(AFOV));
  BlockRAMDualPort #(.AddrBits(4), .Bits(8)) RAM (
    .A(multiplexer_1_out), .Din(multiplexer_2_out), .str(RAMLE), .C(CLK_MAIN), .D(RAM_d));
  PSW PSW (
    .D(pulldown_1_out), .CLK(CLK_MAIN), .CLR(RST), .LE(PSWLE), .SRCALU(PSWFLE), .CYINALU(AFCY),
    .OVINALU(AFOV), .Q({FOV, FCY, FTCMP}));
  Decoder #(.Selector_Bits(2)) decoder_1 (
    .sel(register_with_clear_1_q[9:8]), .out_0(decoder_1_out_0), .out_1(decoder_1_out_1),
    .out_2(decoder_1_out_2), .out_3(decoder_1_out_3));
  assign {pulldown_1_out_2, pulldown_1_out} = RAMOE ? RAM_d : 8'bz;  // Driver driver_1
  Seven_Seg #(.ledPersistence("true"), .commonConnectionType("anode")) seven_seg_1 (
    .a(register_with_clear_2_q[0]), .b(register_with_clear_2_q[1]), .c(register_with_clear_2_q[2]),
    .d(register_with_clear_2_q[3]), .e(register_with_clear_2_q[4]), .f(register_with_clear_2_q[5]),
    .g(register_with_clear_2_q[6]), .dp(register_with_clear_2_q[7]));
  register_with_clear register_with_clear_2 (
    .D(LUTDISP_d), .CLK(CLK_DISPLAY), .CLR(RST), .LE(decoder_1_out_3), .Q(register_with_clear_2_q));
  Seven_Seg #(.ledPersistence("true"), .commonConnectionType("anode")) seven_seg_2 (
    .a(register_with_clear_3_q[0]), .b(register_with_clear_3_q[1]), .c(register_with_clear_3_q[2]),
    .d(register_with_clear_3_q[3]), .e(register_with_clear_3_q[4]), .f(register_with_clear_3_q[5]),
    .g(register_with_clear_3_q[6]), .dp(register_with_clear_3_q[7]));
  register_with_clear register_with_clear_3 (
    .D(LUTDISP_d), .CLK(CLK_DISPLAY), .CLR(RST), .LE(decoder_1_out_2), .Q(register_with_clear_3_q));
  registertriout IR (
    .IO({pulldown_1_out_2, pulldown_1_out}), .CLK(CLK_MAIN), .CLR(RST), .LE(IRLE), .OE(1'b0),
    .DO({IRHO, IR_do}));
  or or_1 (or_1_out, IROE, IRLOE);
  Seven_Seg #(.ledPersistence("true"), .commonConnectionType("anode")) seven_seg_3 (
    .a(register_with_clear_4_q[0]), .b(register_with_clear_4_q[1]), .c(register_with_clear_4_q[2]),
    .d(register_with_clear_4_q[3]), .e(register_with_clear_4_q[4]), .f(register_with_clear_4_q[5]),
    .g(register_with_clear_4_q[6]), .dp(register_with_clear_4_q[7]));
  register_with_clear register_with_clear_4 (
    .D(LUTDISP_d), .CLK(CLK_DISPLAY), .CLR(RST), .LE(decoder_1_out_1), .Q(register_with_clear_4_q));
  assign pulldown_1_out = or_1_out ? IR_do : 4'bz;  // Driver driver_2
  nor nor_1 (AFZF, ADO[0], ADO[1], ADO[2], ADO[3], ADO[4], ADO[5], ADO[6], ADO[7]);
  assign pulldown_1_out_2 = IROE ? IRHO : 4'bz;  // Driver driver_3
  Seven_Seg #(.ledPersistence("true"), .commonConnectionType("anode")) seven_seg_4 (
    .a(register_with_clear_5_q[0]), .b(register_with_clear_5_q[1]), .c(register_with_clear_5_q[2]),
    .d(register_with_clear_5_q[3]), .e(register_with_clear_5_q[4]), .f(register_with_clear_5_q[5]),
    .g(register_with_clear_5_q[6]), .dp(register_with_clear_5_q[7]));
  register_with_clear register_with_clear_5 (
    .D(LUTDISP_d), .CLK(CLK_DISPLAY), .CLR(RST), .LE(decoder_1_out_0), .Q(register_with_clear_5_q));

  // Other names for the same wires on the sheet: PCISn[2:0] = {PCIS2, PCIS1, PCIS0}; CLK = CLK_MAIN;
  //   CLK_DISP = CLK_DISPLAY

  // Notes on the sheet:
  //   CLK_MAIN: Hz: 1000
  //   CLK_DISPLAY: Hz: 240
  //   contents of LUTDECODE0 (hex, n*v repeats v):
  //   29,0,0,0,0,0,0,0,29,44,0,0,0,0,0,0,29,44,0,0,0,0,0,0,29,44,0,0,0,0,0,0,29,44,80,0,
  //   0,0,0,0,29,4,0,0,0,0,0,0,29,4,0,0,0,0,0,0,29,4,0,0,0,0,0,0,29,4,0,0,0,0,0,0,29,4,
  //   0,0,0,0,0,0,29,4,0,0,0,0,0,0,29,0,0,0,0,0,0,0,29,0,0,0,0,0,0,0,29,0,0,0,0,0,0,0,29,
  //   0,0,0,0,0,0,0,29,0,0,0,0,0,0,0,0,0,0,0,0,0,0,0,0,0,3,0,0,0,0,0,0,0,9,22,0,0,0,0,0,
  //   0,9,62,0,0,0,0,0,0,4,0,0,0,0,0,0,2,0,0,0,0,0,0,0,0,0,0,0,0,0,0,0,0,0,0,0,0,0,0,0,
  //   0,0,0,0,0,0,0,0,0,0,0,0,0,0,0,0,0,0,0,0,0,0,0,0,0,0,0,0,0,0,0,0,0,0,0,0,0,0,0,0,0,
  //   0,0,0,0,0,0,0,84,0,0,0,0,0,0,0,0,0,0,0,0,0,0,0,0,0,0,0,0,0,0,0,0,0,0,0,0,0,0,0,0,
  //   0,18,0,0,0,0,0,0,0,18,0,0,0,0,0,0,0,0,0,0,0,0,0,0,0,0,0,0,0,0,0,20,0,0,0,0,0,0,0,
  //   40,0,0,0,0,0,0,0,60,0,0,0,0,0,0,0,80,0,0,0,0,0,0,0,8,0,0,0,0,0,0,0,0,0,0,0,0,0,0,
  //   0,0,0,0,0,0,0,0,0,0,0,0,0,0,0,0,0,0,0,0,0,0,0,0,0,1
  //   contents of LUTDECODE1 (hex, n*v repeats v):
  //   29,0,0,0,0,0,0,0,29,44,0,0,0,0,0,0,29,44,0,0,0,0,0,0,29,44,0,0,0,0,0,0,29,44,80,0,
  //   0,0,0,0,29,4,0,0,0,0,0,0,29,4,0,0,0,0,0,0,29,4,0,0,0,0,0,0,29,4,0,0,0,0,0,0,29,4,
  //   0,0,0,0,0,0,29,4,0,0,0,0,0,0,29,0,0,0,0,0,0,0,29,0,0,0,0,0,0,0,29,0,0,0,0,0,0,0,29,
  //   0,0,0,0,0,0,0,29,0,0,0,0,0,0,0,0,0,0,0,0,0,0,0,0,0,3,0,0,0,0,0,0,0,9,22,0,0,0,0,0,
  //   0,9,62,0,0,0,0,0,0,4,0,0,0,0,0,0,2,0,0,0,0,0,0,0,0,0,0,0,0,0,0,0,0,0,0,0,0,0,0,0,
  //   0,0,0,0,0,0,0,0,0,0,0,0,0,0,0,0,0,0,0,0,0,0,0,0,0,0,0,0,0,0,0,0,0,0,0,0,0,0,0,0,0,
  //   0,0,0,0,0,0,0,84,0,0,0,0,0,0,0,0,0,0,0,0,0,0,0,0,0,0,0,0,0,0,0,0,0,0,0,0,0,0,0,0,
  //   0,18,0,0,0,0,0,0,0,18,0,0,0,0,0,0,0,0,0,0,0,0,0,0,0,0,0,0,0,0,0,20,0,0,0,0,0,0,0,
  //   40,0,0,0,0,0,0,0,60,0,0,0,0,0,0,0,80,0,0,0,0,0,0,0,8,0,0,0,0,0,0,0,0,0,0,0,0,0,0,
  //   0,0,0,0,0,0,0,0,0,0,0,0,0,0,0,0,0,0,0,0,0,0,0,0,0,1
  //   contents of LUTDECODE2 (hex, n*v repeats v):
  //   29,0,0,0,0,0,0,0,29,44,0,0,0,0,0,0,29,44,0,0,0,0,0,0,29,44,0,0,0,0,0,0,29,44,80,0,
  //   0,0,0,0,29,4,0,0,0,0,0,0,29,4,0,0,0,0,0,0,29,4,0,0,0,0,0,0,29,4,0,0,0,0,0,0,29,4,
  //   0,0,0,0,0,0,29,4,0,0,0,0,0,0,29,0,0,0,0,0,0,0,29,0,0,0,0,0,0,0,29,0,0,0,0,0,0,0,29,
  //   0,0,0,0,0,0,0,29,0,0,0,0,0,0,0,0,0,0,0,0,0,0,0,0,0,3,0,0,0,0,0,0,0,9,22,0,0,0,0,0,
  //   0,9,62,0,0,0,0,0,0,4,0,0,0,0,0,0,2,0,0,0,0,0,0,0,0,0,0,0,0,0,0,0,0,0,0,0,0,0,0,0,
  //   0,0,0,0,0,0,0,0,0,0,0,0,0,0,0,0,0,0,0,0,0,0,0,0,0,0,0,0,0,0,0,0,0,0,0,0,0,0,0,0,0,
  //   0,0,0,0,0,0,0,84,0,0,0,0,0,0,0,0,0,0,0,0,0,0,0,0,0,0,0,0,0,0,0,0,0,0,0,0,0,0,0,0,
  //   0,18,0,0,0,0,0,0,0,18,0,0,0,0,0,0,0,0,0,0,0,0,0,0,0,0,0,0,0,0,0,20,0,0,0,0,0,0,0,
  //   40,0,0,0,0,0,0,0,60,0,0,0,0,0,0,0,80,0,0,0,0,0,0,0,8,0,0,0,0,0,0,0,0,0,0,0,0,0,0,
  //   0,0,0,0,0,0,0,0,0,0,0,0,0,0,0,0,0,0,0,0,0,0,0,0,0,1
  //   contents of ROM (hex, n*v repeats v):
  //   a9,51,40,50,e0,20,78,64,e0,30,84,68
  //   contents of LUTDISP (hex, n*v repeats v):
  //   3f,6,5b,4f,66,6d,7d,7,7f,6f,3f,6,5b,4f,66,6d,7d,7,7f,6f,3f,6,5b,4f,66,6d,7d,7,7f,
  //   6f,3f,6,5b,4f,66,6d,7d,7,7f,6f,3f,6,5b,4f,66,6d,7d,7,7f,6f,3f,6,5b,4f,66,6d,7d,7,
  //   7f,6f,3f,6,5b,4f,66,6d,7d,7,7f,6f,3f,6,5b,4f,66,6d,7d,7,7f,6f,3f,6,5b,4f,66,6d,7d,
  //   7,7f,6f,3f,6,5b,4f,66,6d,7d,7,7f,6f,3f,6,5b,4f,66,6d,7d,7,7f,6f,3f,6,5b,4f,66,6d,
  //   7d,7,7f,6f,3f,6,5b,4f,66,6d,7d,7,7f,6f,3f,6,5b,4f,66,6d,7d,7,7f,6f,3f,6,5b,4f,66,
  //   6d,7d,7,7f,6f,3f,6,5b,4f,66,6d,7d,7,7f,6f,3f,6,5b,4f,66,6d,7d,7,7f,6f,3f,6,5b,4f,
  //   66,6d,7d,7,7f,6f,3f,6,5b,4f,66,6d,7d,7,7f,6f,3f,6,5b,4f,66,6d,7d,7,7f,6f,3f,6,5b,
  //   4f,66,6d,7d,7,7f,6f,3f,6,5b,4f,66,6d,7d,7,7f,6f,3f,6,5b,4f,66,6d,7d,7,7f,6f,3f,6,
  //   5b,4f,66,6d,7d,7,7f,6f,3f,6,5b,4f,66,6d,7d,7,7f,6f,3f,6,5b,4f,66,6d,3f,3f,3f,3f,3f,
  //   3f,3f,3f,3f,3f,6,6,6,6,6,6,6,6,6,6,5b,5b,5b,5b,5b,5b,5b,5b,5b,5b,4f,4f,4f,4f,4f,4f,
  //   4f,4f,4f,4f,66,66,66,66,66,66,66,66,66,66,6d,6d,6d,6d,6d,6d,6d,6d,6d,6d,7d,7d,7d,
  //   7d,7d,7d,7d,7d,7d,7d,7,7,7,7,7,7,7,7,7,7,7f,7f,7f,7f,7f,7f,7f,7f,7f,7f,6f,6f,6f,6f,
  //   6f,6f,6f,6f,6f,6f,3f,3f,3f,3f,3f,3f,3f,3f,3f,3f,6,6,6,6,6,6,6,6,6,6,5b,5b,5b,5b,5b,
  //   5b,5b,5b,5b,5b,4f,4f,4f,4f,4f,4f,4f,4f,4f,4f,66,66,66,66,66,66,66,66,66,66,6d,6d,
  //   6d,6d,6d,6d,6d,6d,6d,6d,7d,7d,7d,7d,7d,7d,7d,7d,7d,7d,7,7,7,7,7,7,7,7,7,7,7f,7f,7f,
  //   7f,7f,7f,7f,7f,7f,7f,6f,6f,6f,6f,6f,6f,6f,6f,6f,6f,3f,3f,3f,3f,3f,3f,3f,3f,3f,3f,
  //   6,6,6,6,6,6,6,6,6,6,5b,5b,5b,5b,5b,5b,5b,5b,5b,5b,4f,4f,4f,4f,4f,4f,4f,4f,4f,4f,66,
  //   66,66,66,66,66,66,66,66,66,6d,6d,6d,6d,6d,6d,3f,3f,3f,3f,3f,3f,3f,3f,3f,3f,3f,3f,
  //   3f,3f,3f,3f,3f,3f,3f,3f,3f,3f,3f,3f,3f,3f,3f,3f,3f,3f,3f,3f,3f,3f,3f,3f,3f,3f,3f,
  //   3f,3f,3f,3f,3f,3f,3f,3f,3f,3f,3f,3f,3f,3f,3f,3f,3f,3f,3f,3f,3f,3f,3f,3f,3f,3f,3f,
  //   3f,3f,3f,3f,3f,3f,3f,3f,3f,3f,3f,3f,3f,3f,3f,3f,3f,3f,3f,3f,3f,3f,3f,3f,3f,3f,3f,
  //   3f,3f,3f,3f,3f,3f,3f,6,6,6,6,6,6,6,6,6,6,6,6,6,6,6,6,6,6,6,6,6,6,6,6,6,6,6,6,6,6,
  //   6,6,6,6,6,6,6,6,6,6,6,6,6,6,6,6,6,6,6,6,6,6,6,6,6,6,6,6,6,6,6,6,6,6,6,6,6,6,6,6,6,
  //   6,6,6,6,6,6,6,6,6,6,6,6,6,6,6,6,6,6,6,6,6,6,6,6,6,6,6,6,6,5b,5b,5b,5b,5b,5b,5b,5b,
  //   5b,5b,5b,5b,5b,5b,5b,5b,5b,5b,5b,5b,5b,5b,5b,5b,5b,5b,5b,5b,5b,5b,5b,5b,5b,5b,5b,
  //   5b,5b,5b,5b,5b,5b,5b,5b,5b,5b,5b,5b,5b,5b,5b,5b,5b,5b,5b,5b,5b,0,0,0,0,0,0,0,0,0,
  //   0,0,0,0,0,0,0,0,0,0,0,0,0,0,0,0,0,0,0,0,0,0,0,0,0,0,0,0,0,0,0,0,0,0,0,0,0,0,0,0,0,
  //   0,0,0,0,0,0,0,0,0,0,0,0,0,0,0,0,0,0,0,0,0,0,0,0,0,0,0,0,0,0,0,0,0,0,0,0,0,0,0,0,0,
  //   0,0,0,0,0,0,0,0,0,0,0,0,0,0,0,0,0,0,0,0,0,0,0,0,0,0,0,0,0,0,0,0,0,0,0,0,0,0,0,0,0,
  //   0,0,0,0,0,0,0,0,0,0,0,0,0,0,0,0,0,0,0,0,0,0,0,0,0,0,0,0,0,0,0,0,0,0,0,0,0,0,0,0,0,
  //   0,0,0,0,0,0,0,0,0,0,0,0,0,0,0,0,0,0,0,0,0,0,0,0,0,0,0,0,0,0,0,0,0,0,0,0,0,0,0,0,0,
  //   0,0,0,0,0,0,0,0,0,0,0,0,0,0,0,0,0,0,0,0,0,0,0,0,0,0,0,0,0,0,0,0,0,0,0,0,0,0,0,0,0,
  //   0,3f,6,5b,4f,66,6d,7d,7,7f,6f,3f,6,5b,4f,66,6d,7d,7,7f,6f,3f,6,5b,4f,66,6d,7d,7,7f,
  //   6f,3f,6,5b,4f,66,6d,7d,7,7f,6f,3f,6,5b,4f,66,6d,7d,7,7f,6f,3f,6,5b,4f,66,6d,7d,7,
  //   7f,6f,3f,6,5b,4f,66,6d,7d,7,7f,6f,3f,6,5b,4f,66,6d,7d,7,7f,6f,3f,6,5b,4f,66,6d,7d,
  //   7,7f,6f,3f,6,5b,4f,66,6d,7d,7,7f,6f,3f,6,5b,4f,66,6d,7d,7,7f,6f,3f,6,5b,4f,66,6d,
  //   7d,7,7f,6f,3f,6,5b,4f,66,6d,7d,7,7f,7,7d,6d,66,4f,5b,6,3f,6f,7f,7,7d,6d,66,4f,5b,
  //   6,3f,6f,7f,7,7d,6d,66,4f,5b,6,3f,6f,7f,7,7d,6d,66,4f,5b,6,3f,6f,7f,7,7d,6d,66,4f,
  //   5b,6,3f,6f,7f,7,7d,6d,66,4f,5b,6,3f,6f,7f,7,7d,6d,66,4f,5b,6,3f,6f,7f,7,7d,6d,66,
  //   4f,5b,6,3f,6f,7f,7,7d,6d,66,4f,5b,6,3f,6f,7f,7,7d,6d,66,4f,5b,6,3f,6f,7f,7,7d,6d,
  //   66,4f,5b,6,3f,6f,7f,7,7d,6d,66,4f,5b,6,3f,6f,7f,7,7d,6d,66,4f,5b,6,3f,3f,3f,3f,3f,
  //   3f,3f,3f,3f,3f,6,6,6,6,6,6,6,6,6,6,5b,5b,5b,5b,5b,5b,5b,5b,5b,5b,4f,4f,4f,4f,4f,4f,
  //   4f,4f,4f,4f,66,66,66,66,66,66,66,66,66,66,6d,6d,6d,6d,6d,6d,6d,6d,6d,6d,7d,7d,7d,
  //   7d,7d,7d,7d,7d,7d,7d,7,7,7,7,7,7,7,7,7,7,7f,7f,7f,7f,7f,7f,7f,7f,7f,7f,6f,6f,6f,6f,
  //   6f,6f,6f,6f,6f,6f,3f,3f,3f,3f,3f,3f,3f,3f,3f,3f,6,6,6,6,6,6,6,6,6,6,5b,5b,5b,5b,5b,
  //   5b,5b,5b,5b,5b,5b,5b,5b,5b,5b,5b,5b,6,6,6,6,6,6,6,6,6,6,3f,3f,3f,3f,3f,3f,3f,3f,3f,
  //   3f,6f,6f,6f,6f,6f,6f,6f,6f,6f,6f,7f,7f,7f,7f,7f,7f,7f,7f,7f,7f,7,7,7,7,7,7,7,7,7,
  //   7,7d,7d,7d,7d,7d,7d,7d,7d,7d,7d,6d,6d,6d,6d,6d,6d,6d,6d,6d,6d,66,66,66,66,66,66,66,
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endmodule
