// Digital circuit ALU.dig as structural Verilog
module ALU (
  input  [7:0] B,
  input  [7:0] A,
  input  SUB,
  input  OE,
  output [7:0] Y,
  output CY,
  output OV
);

  wire ADDER_c_o, and_1_out, nor_1_out, not_1_out, xor_3_out;
  wire [7:0] ADDER_s, xor_1_out;

  assign xor_1_out = B ^ {8{SUB}};  // XOr xor_1, 8 bits wide
  Add #(.Bits(8)) ADDER (.a(A), .b(xor_1_out), .c_i(SUB), .s(ADDER_s), .c_o(ADDER_c_o));
  assign Y = OE ? ADDER_s : 8'bz;  // Driver driver_1
  xor xor_2 (CY, ADDER_c_o, SUB);
  xor xor_3 (xor_3_out, SUB, B[7]);
  not not_1 (not_1_out, ADDER_s[7]);
  nor nor_1 (nor_1_out, not_1_out, A[7], xor_3_out);
  and and_1 (and_1_out, not_1_out, A[7], xor_3_out);
  or or_1 (OV, nor_1_out, and_1_out);
endmodule
