// Digital circuit IR.dig as structural Verilog
module IR (
  input  [7:0] IO,
  input  CLK,
  input  CLR,
  input  LE,
  input  LOE,
  input  HOE,
  output [7:0] DO
);

  register_with_clear register_with_clear_1 (.D(IO), .CLK(CLK), .CLR(CLR), .LE(LE), .Q(DO));
  assign IO[3:0] = LOE ? DO[3:0] : 4'bz;  // Driver driver_1
  assign IO[7:4] = HOE ? DO[7:4] : 4'bz;  // Driver driver_2
endmodule
