// Digital circuit PC.dig as structural Verilog
module PC (
  input  [7:0] IO,
  input  CLK,
  input  CLR,
  input  OE,
  input  CE,
  input  [2:0] LES,
  input  FCY,
  input  FOV,
  input  FZF,
  output [7:0] DO
);

  wire multiplexer_1_out;

  Multiplexer #(.Selector_Bits(3)) multiplexer_1 (
    .sel(LES), .in_0(1'b0), .in_1(1'b1), .in_2(FCY), .in_3(FZF), .in_4(FOV), .in_5(1'b0), .in_6(1'b0),
    .in_7(1'b0), .out(multiplexer_1_out));
  CounterPreset #(.Bits(8)) counterpreset_1 (
    .en(CE), .C(CLK), .dir(1'b0), .in(IO), .ld(multiplexer_1_out), .clr(CLR), .out(DO));  // open: ovf
  assign IO = OE ? DO : 8'bz;  // Driver driver_1
endmodule
