// Digital circuit PSW.dig as structural Verilog
module PSW (
  input  [3:0] D,
  input  CLK,
  input  CLR,
  input  LE,
  input  SRCALU,
  input  CYINALU,
  input  OVINALU,
  output [2:0] Q
);

  wire multiplexer_1_out, multiplexer_2_out, multiplexer_3_out, multiplexer_4_out, multiplexer_5_out,
       multiplexer_6_out, multiplexer_7_out, multiplexer_8_out, multiplexer_9_out, or_1_out;

  Multiplexer multiplexer_1 (.sel(D[0]), .in_0(Q[0]), .in_1(D[3]), .out(multiplexer_1_out));
  Multiplexer multiplexer_2 (.sel(D[1]), .in_0(Q[1]), .in_1(D[3]), .out(multiplexer_2_out));
  Multiplexer multiplexer_3 (.sel(D[2]), .in_0(Q[2]), .in_1(D[3]), .out(multiplexer_3_out));
  Multiplexer multiplexer_4 (.sel(SRCALU), .in_0(multiplexer_1_out), .in_1(Q[0]), .out(multiplexer_4_out));
  Multiplexer multiplexer_5 (.sel(SRCALU), .in_0(multiplexer_2_out), .in_1(CYINALU), .out(multiplexer_5_out));
  Multiplexer multiplexer_6 (.sel(SRCALU), .in_0(multiplexer_3_out), .in_1(OVINALU), .out(multiplexer_6_out));
  Multiplexer multiplexer_7 (.sel(CLR), .in_0(multiplexer_4_out), .in_1(1'b0), .out(multiplexer_7_out));
  Multiplexer multiplexer_8 (.sel(CLR), .in_0(multiplexer_5_out), .in_1(1'b0), .out(multiplexer_8_out));
  Multiplexer multiplexer_9 (.sel(CLR), .in_0(multiplexer_6_out), .in_1(1'b0), .out(multiplexer_9_out));
  or or_1 (or_1_out, CLR, LE);
  Register register_1 (.D(multiplexer_7_out), .C(CLK), .en(or_1_out), .Q(Q[0]));
  Register register_2 (.D(multiplexer_8_out), .C(CLK), .en(or_1_out), .Q(Q[1]));
  Register register_3 (.D(multiplexer_9_out), .C(CLK), .en(or_1_out), .Q(Q[2]));
endmodule
