// Digital circuit core.dig as structural Verilog
module core (
  input  CLK,
  input  RST,
  input  [7:0] BUS,
  output OUTLE,
  output [3:0] EADDR
);

  wire ADDRLE, AFCY, AFOV, AFZF, ALE, ALUOE, ALUSUB, AOE, BLE, BOE, FCY, FOV, FTCMP, HALT, IRHOE, IRLE,
       IRLOE, ManualRAM, not_1_out, PCCE, PCIS0, PCIS1, PCIS2, PCOE, PSWFLE, PSWLE, RAMLE, RAMOE, RESERVED0,
       RESERVED1, ROMOE;
  wire [2:0] MCIO;
  wire [3:0] IRHDO, ManualRAMAddr, multiplexer_1_out, RAR_q;
  wire [7:0] ADO, BDO, ManualRAMData, multiplexer_2_out, PC_do, RAM_d;

  Counter #(.Bits(3)) counter_1 (.en(1'b1), .C(CLK), .clr(RST), .out(MCIO));  // open: ovf
  EEPROM #(.AddrBits(13), .isProgramMemory("true"), .Bits(8)) LUTDECODE0 (
    .A({{6{1'b0}}, IRHDO, MCIO}), .CS(~1'b0), .WE(~1'b1), .OE(~1'b0),
    .D({RAMLE, ADDRLE, PCCE, PCOE, ROMOE, IRLOE, IRHOE, IRLE}));
  EEPROM #(.AddrBits(13), .isProgramMemory("true"), .Bits(8)) LUTDECODE1 (
    .A({6'b000001, IRHDO, MCIO}), .CS(~1'b0), .WE(~1'b1), .OE(~1'b0),
    .D({OUTLE, ALUSUB, ALUOE, BOE, BLE, AOE, ALE, RAMOE}));
  EEPROM #(.AddrBits(13), .isProgramMemory("true"), .Bits(8)) LUTDECODE2 (
    .A({6'b000010, IRHDO, MCIO}), .CS(~1'b0), .WE(~1'b1), .OE(~1'b0),
    .D({PCIS2, PCIS1, PCIS0, PSWFLE, PSWLE, RESERVED1, RESERVED0, HALT}));
  DipSwitch dipswitch_1 (.out(ManualRAM));
  DipSwitch dipswitch_2 (.out(ManualRAMData[0]));
  DipSwitch dipswitch_3 (.out(ManualRAMData[1]));
  DipSwitch dipswitch_4 (.out(ManualRAMData[2]));
  DipSwitch dipswitch_5 (.out(ManualRAMData[3]));
  DipSwitch dipswitch_6 (.out(ManualRAMData[4]));
  DipSwitch dipswitch_7 (.out(ManualRAMData[5]));
  DipSwitch dipswitch_8 (.out(ManualRAMData[6]));
  DipSwitch dipswitch_9 (.out(ManualRAMData[7]));
  DipSwitch dipswitch_10 (.out(ManualRAMAddr[0]));
  DipSwitch dipswitch_11 (.out(ManualRAMAddr[1]));
  DipSwitch dipswitch_12 (.out(ManualRAMAddr[2]));
  DipSwitch dipswitch_13 (.out(ManualRAMAddr[3]));
  // Probe on IRLE
  // Probe on IRHOE
  // Probe on IRLOE
  // Probe on ROMOE
  // Probe on PCOE
  // Probe on PCCE
  // Probe on ADDRLE
  // Probe on RAMLE
  // Probe on RAMOE
  // Probe on ALE
  // Probe on AOE
  // Probe on BLE
  // Probe on BOE
  // Probe on ALUOE
  // Probe on ALUSUB
  // Probe on OUTLE
  // Probe on HALT
  // Probe on RESERVED0
  // Probe on RESERVED1
  // Probe on PSWLE
  // Probe on PSWFLE
  // Probe on PCIS0
  // Probe on PCIS1
  // Probe on PCIS2
  // Probe on MCIO
  // Probe on ADO
  // Probe on BDO
  // Probe on BDO
  PullDown #(.Bits(8)) pulldown_1 (.out(BUS));
  registertriout REGA (.IO(BUS), .CLK(CLK), .CLR(RST), .LE(ALE), .OE(AOE), .DO(ADO));
  Register #(.Bits(4)) RAR (.D(BUS[3:0]), .C(CLK), .en(ADDRLE), .Q(RAR_q));
  PC PC (
    .IO(BUS), .CLK(CLK), .CLR(RST), .OE(PCOE), .CE(PCCE), .LES({PCIS2, PCIS1, PCIS0}), .FCY(FCY), .FOV(FOV),
    .FZF(AFZF), .DO(PC_do));
  registertriout REGB (.IO(BUS), .CLK(CLK), .CLR(RST), .LE(BLE), .OE(BOE), .DO(BDO));
  EEPROM #(.AddrBits(8), .isProgramMemory("true"), .Bits(8)) ROM (
    .A(PC_do), .CS(~1'b0), .WE(~1'b1), .OE(~not_1_out), .D(BUS));
  not not_1 (not_1_out, ROMOE);
  Multiplexer #(.Bits(4)) multiplexer_1 (.sel(ManualRAM), .in_0(RAR_q), .in_1(ManualRAMAddr), .out(multiplexer_1_out));
  Multiplexer #(.Bits(8)) multiplexer_2 (.sel(ManualRAM), .in_0(BUS), .in_1(ManualRAMData), .out(multiplexer_2_out));
  ALU alu_1 (.OE(ALUOE), .A(ADO), .B(BDO), .SUB(ALUSUB), .Y(BUS), .CY(AFCY), .OV(AFOV));
  BlockRAMDualPort #(.AddrBits(4), .Bits(8)) RAM (
    .A(multiplexer_1_out), .Din(multiplexer_2_out), .str(RAMLE), .C(CLK), .D(RAM_d));
  PSW PSW (
    .D(BUS[3:0]), .CLK(CLK), .CLR(RST), .LE(PSWLE), .SRCALU(PSWFLE), .CYINALU(AFCY), .OVINALU(AFOV),
    .Q({FOV, FCY, FTCMP}));
  assign BUS = RAMOE ? RAM_d : 8'bz;  // Driver driver_1
  // Probe on RAM_d
  IR IR (.IO(BUS), .CLK(CLK), .CLR(RST), .LE(IRLE), .LOE(IRLOE), .HOE(IRHOE), .DO({IRHDO, EADDR}));
  nor nor_1 (AFZF, ADO[0], ADO[1], ADO[2], ADO[3], ADO[4], ADO[5], ADO[6], ADO[7]);

  // Other names for the same wires on the sheet: PCISn[2:0] = {PCIS2, PCIS1, PCIS0}; IRLDO[3:0] = EADDR

  // Notes on the sheet:
  //   contents of LUTDECODE0 (hex, n*v repeats v):
  //   29,0,0,0,0,0,0,0,29,44,0,0,0,0,0,0,29,44,0,0,0,0,0,0,29,44,0,0,0,0,0,0,29,44,80,0,
  //   0,0,0,0,29,4,0,0,0,0,0,0,29,4,0,0,0,0,0,0,29,4,0,0,0,0,0,0,29,4,0,0,0,0,0,0,29,4,
  //   0,0,0,0,0,0,29,4,0,0,0,0,0,0,29,0,0,0,0,0,0,0,29,0,0,0,0,0,0,0,29,0,0,0,0,0,0,0,29,
  //   0,0,0,0,0,0,0,29,0,0,0,0,0,0,0,0,0,0,0,0,0,0,0,0,0,3,0,0,0,0,0,0,0,9,22,0,0,0,0,0,
  //   0,9,62,0,0,0,0,0,0,4,0,0,0,0,0,0,2,0,0,0,0,0,0,0,0,0,0,0,0,0,0,0,0,0,0,0,0,0,0,0,
  //   0,0,0,0,0,0,0,0,0,0,0,0,0,0,0,0,0,0,0,0,0,0,0,0,0,0,0,0,0,0,0,0,0,0,0,0,0,0,0,0,0,
  //   0,0,0,0,0,0,0,84,0,0,0,0,0,0,0,0,0,0,0,0,0,0,0,0,0,0,0,0,0,0,0,0,0,0,0,0,0,0,0,0,
  //   0,18,0,0,0,0,0,0,0,18,0,0,0,0,0,0,0,0,0,0,0,0,0,0,0,0,0,0,0,0,0,20,0,0,0,0,0,0,0,
  //   40,0,0,0,0,0,0,0,60,0,0,0,0,0,0,0,80,0,0,0,0,0,0,0,8,0,0,0,0,0,0,0,0,0,0,0,0,0,0,
  //   0,0,0,0,0,0,0,0,0,0,0,0,0,0,0,0,0,0,0,0,0,0,0,0,0,1
  //   contents of LUTDECODE1 (hex, n*v repeats v):
  //   29,0,0,0,0,0,0,0,29,44,0,0,0,0,0,0,29,44,0,0,0,0,0,0,29,44,0,0,0,0,0,0,29,44,80,0,
  //   0,0,0,0,29,4,0,0,0,0,0,0,29,4,0,0,0,0,0,0,29,4,0,0,0,0,0,0,29,4,0,0,0,0,0,0,29,4,
  //   0,0,0,0,0,0,29,4,0,0,0,0,0,0,29,0,0,0,0,0,0,0,29,0,0,0,0,0,0,0,29,0,0,0,0,0,0,0,29,
  //   0,0,0,0,0,0,0,29,0,0,0,0,0,0,0,0,0,0,0,0,0,0,0,0,0,3,0,0,0,0,0,0,0,9,22,0,0,0,0,0,
  //   0,9,62,0,0,0,0,0,0,4,0,0,0,0,0,0,2,0,0,0,0,0,0,0,0,0,0,0,0,0,0,0,0,0,0,0,0,0,0,0,
  //   0,0,0,0,0,0,0,0,0,0,0,0,0,0,0,0,0,0,0,0,0,0,0,0,0,0,0,0,0,0,0,0,0,0,0,0,0,0,0,0,0,
  //   0,0,0,0,0,0,0,84,0,0,0,0,0,0,0,0,0,0,0,0,0,0,0,0,0,0,0,0,0,0,0,0,0,0,0,0,0,0,0,0,
  //   0,18,0,0,0,0,0,0,0,18,0,0,0,0,0,0,0,0,0,0,0,0,0,0,0,0,0,0,0,0,0,20,0,0,0,0,0,0,0,
  //   40,0,0,0,0,0,0,0,60,0,0,0,0,0,0,0,80,0,0,0,0,0,0,0,8,0,0,0,0,0,0,0,0,0,0,0,0,0,0,
  //   0,0,0,0,0,0,0,0,0,0,0,0,0,0,0,0,0,0,0,0,0,0,0,0,0,1
  //   contents of LUTDECODE2 (hex, n*v repeats v):
  //   29,0,0,0,0,0,0,0,29,44,0,0,0,0,0,0,29,44,0,0,0,0,0,0,29,44,0,0,0,0,0,0,29,44,80,0,
  //   0,0,0,0,29,4,0,0,0,0,0,0,29,4,0,0,0,0,0,0,29,4,0,0,0,0,0,0,29,4,0,0,0,0,0,0,29,4,
  //   0,0,0,0,0,0,29,4,0,0,0,0,0,0,29,0,0,0,0,0,0,0,29,0,0,0,0,0,0,0,29,0,0,0,0,0,0,0,29,
  //   0,0,0,0,0,0,0,29,0,0,0,0,0,0,0,0,0,0,0,0,0,0,0,0,0,3,0,0,0,0,0,0,0,9,22,0,0,0,0,0,
  //   0,9,62,0,0,0,0,0,0,4,0,0,0,0,0,0,2,0,0,0,0,0,0,0,0,0,0,0,0,0,0,0,0,0,0,0,0,0,0,0,
  //   0,0,0,0,0,0,0,0,0,0,0,0,0,0,0,0,0,0,0,0,0,0,0,0,0,0,0,0,0,0,0,0,0,0,0,0,0,0,0,0,0,
  //   0,0,0,0,0,0,0,84,0,0,0,0,0,0,0,0,0,0,0,0,0,0,0,0,0,0,0,0,0,0,0,0,0,0,0,0,0,0,0,0,
  //   0,18,0,0,0,0,0,0,0,18,0,0,0,0,0,0,0,0,0,0,0,0,0,0,0,0,0,0,0,0,0,20,0,0,0,0,0,0,0,
  //   40,0,0,0,0,0,0,0,60,0,0,0,0,0,0,0,80,0,0,0,0,0,0,0,8,0,0,0,0,0,0,0,0,0,0,0,0,0,0,
  //   0,0,0,0,0,0,0,0,0,0,0,0,0,0,0,0,0,0,0,0,0,0,0,0,0,1
  //   contents of ROM (hex, n*v repeats v):
  //   51,e1,40,50,e0,20,78,64,e0,30,84,68
endmodule
