// Digital circuit register_with_clear.dig as structural Verilog
module register_with_clear (
  input  [7:0] D,
  input  CLK,
  input  CLR,
  input  LE,
  output [7:0] Q
);

  wire or_1_out;
  wire [7:0] multiplexer_1_out;

  Multiplexer #(.Bits(8)) multiplexer_1 (.sel(CLR), .in_0(D), .in_1({8{1'b0}}), .out(multiplexer_1_out));
  or or_1 (or_1_out, CLR, LE);
  Register #(.Bits(8)) register_1 (.D(multiplexer_1_out), .C(CLK), .en(or_1_out), .Q(Q));
endmodule
