// Digital circuit registertriout.dig as structural Verilog
module registertriout (
  input  [7:0] IO,
  input  CLK,
  input  CLR,
  input  LE,
  input  OE,
  output [7:0] DO
);

  register_with_clear register_with_clear_1 (.D(IO), .CLK(CLK), .CLR(CLR), .LE(LE), .Q(DO));
  assign IO = OE ? DO : 8'bz;  // Driver driver_1
endmodule
